// Logisim project Group_05_Problem_03.circ as structural Verilog: 1 circuit, main circuit main
module main (
  input  A,
  input  B,
  input  C,
  output LED1,
  output LED0
);

  wire n7404_1_p2, n7404_1_p8, n7404_1_p9, n7404_1_p10, n7408_1_p3, n7408_1_p6, n7408_1_p11, n7408_1_p12,
       n7408_1_p14, n7408_2_p3, n7408_2_p6, n7408_2_p11;

  // _7408 7408_1: pin names not known; wires that end beside it: A, B, n7408_1_p3, B, C, n7408_1_p6, 1'b0, 1'b1, A, C, n7408_1_p11, n7408_1_p12, C, n7408_1_p14
  // _7404 7404_1: pin names not known; wires that end beside it: A, n7404_1_p2, B, n7408_1_p12, 1'b0, 1'b1, C, n7404_1_p8, n7404_1_p9, n7404_1_p10
  // _7408 7408_2: pin names not known; wires that end beside it: B, n7404_1_p8, n7408_2_p3, n7404_1_p10, A, n7408_2_p6, 1'b0, 1'b1, n7404_1_p2, n7404_1_p9, n7408_2_p11
  // _7432 7432_1: pin names not known; wires that end beside it: n7408_1_p11, n7408_1_p6, n7408_1_p3, LED1, 1'b0, 1'b1, n7408_1_p14, n7408_2_p3, n7404_1_p9, n7408_2_p11, n7408_2_p6, LED0
endmodule
