// Logisim project Group_05_Problem_04.circ as structural Verilog: 1 circuit, main circuit main
module main (
  input  A,
  input  B,
  input  C,
  input  D,
  output Result
);

  wire A_prime_BCD_prime_p1, A_prime_BCD_prime_p3, A_prime_BCD_prime_p6, A_prime_BCD_prime_p10,
       A_prime_BCD_prime_p11, AB_prime_C_prime_D_p2, AB_prime_C_prime_D_p3, AB_prime_C_prime_D_p5,
       AB_prime_C_prime_D_p6, AB_prime_C_prime_D_p11, ABC_prime_D_prime_p3, ABC_prime_D_prime_p6,
       ABC_prime_D_prime_p11, ABCD_p3, ABCD_p6, ABCD_p11, n7432_1_p3, n7432_1_p6;

  // _7408 AB_prime_C_prime_D: pin names not known; wires that end beside it: A, AB_prime_C_prime_D_p2, AB_prime_C_prime_D_p3, AB_prime_C_prime_D_p3, AB_prime_C_prime_D_p5, AB_prime_C_prime_D_p6, 1'b0, 1'b1, AB_prime_C_prime_D_p6, D, AB_prime_C_prime_D_p11
  // _7408 A_prime_BCD_prime: pin names not known; wires that end beside it: A_prime_BCD_prime_p1, B, A_prime_BCD_prime_p3, A_prime_BCD_prime_p3, C, A_prime_BCD_prime_p6, 1'b0, 1'b1, A_prime_BCD_prime_p6, A_prime_BCD_prime_p10, A_prime_BCD_prime_p11
  // _7404 7404_1: pin names not known; wires that end beside it: A, A_prime_BCD_prime_p1, B, AB_prime_C_prime_D_p2, 1'b0, 1'b1, C, AB_prime_C_prime_D_p5, D, A_prime_BCD_prime_p10
  // _7408 ABCD: pin names not known; wires that end beside it: A, B, ABCD_p3, ABCD_p3, C, ABCD_p6, 1'b0, 1'b1, ABCD_p6, D, ABCD_p11, 1'b1
  // _7408 ABC_prime_D_prime: pin names not known; wires that end beside it: A, B, ABC_prime_D_prime_p3, ABC_prime_D_prime_p3, AB_prime_C_prime_D_p5, ABC_prime_D_prime_p6, 1'b0, 1'b1, ABC_prime_D_prime_p6, A_prime_BCD_prime_p10, ABC_prime_D_prime_p11
  // _7432 7432_1: pin names not known; wires that end beside it: AB_prime_C_prime_D_p11, A_prime_BCD_prime_p11, n7432_1_p3, n7432_1_p3, ABC_prime_D_prime_p11, n7432_1_p6, 1'b0, 1'b1, n7432_1_p6, ABCD_p11, Result, 1'b0
endmodule
