// Logisim project Group_5_Problem_1.circ as structural Verilog: 1 circuit, main circuit main
module main (
  input  A,
  input  B,
  input  C,
  input  D,
  output Y
);

  wire n7408_1_p2, n7408_1_p3, n7408_1_p4, n7408_1_p7;

  // _7408 7408_1: pin names not known; wires that end beside it: A, n7408_1_p2, n7408_1_p3, n7408_1_p4, B, D, n7408_1_p7
  // _7432 7432_1: pin names not known; wires that end beside it: n7408_1_p7, n7408_1_p4, Y, C
  // _7404 7404_1: pin names not known; wires that end beside it: B, n7408_1_p2, D, n7408_1_p3
endmodule
