// Logisim project Group -05,problem-01 using basic gates.circ as structural Verilog: 1 circuit, main circuit main
module main (
  input  P1,
  input  P0,
  input  Q1,
  input  Q0,
  output L,
  output E,
  output G
);

  wire and_1_out, and_2_out, and_3_out, and_4_out, and_5_out, and_6_out, and_7_out, and_8_out, and_9_out,
       and_10_out, and_11_out, and_12_out, and_13_out, and_14_out, and_15_out, and_16_out, and_17_out,
       and_18_out, and_19_out, and_20_out, and_21_out, and_22_out, not_1_out, not_2_out, not_3_out,
       not_4_out, or_1_out, or_3_out, or_4_out, or_6_out;

  not not_1 (not_1_out, P1);
  not not_2 (not_2_out, P0);
  not not_3 (not_3_out, Q1);
  not not_4 (not_4_out, Q0);
  and and_1 (and_1_out, P1, not_3_out);
  and and_2 (and_2_out, P1, P0);
  and and_3 (and_3_out, P0, not_3_out);
  and and_4 (and_4_out, and_2_out, not_4_out);
  and and_5 (and_5_out, and_3_out, not_4_out);
  or or_1 (or_1_out, and_1_out, and_4_out);
  or or_2 (G, or_1_out, and_5_out);
  and and_6 (and_6_out, P1, P0);
  and and_7 (and_7_out, Q1, Q0);
  and and_8 (and_8_out, not_1_out, not_3_out);
  and and_9 (and_9_out, P0, Q0);
  and and_10 (and_10_out, not_2_out, not_4_out);
  and and_11 (and_11_out, P1, Q1);
  and and_12 (and_12_out, not_1_out, not_2_out);
  and and_13 (and_13_out, not_3_out, not_4_out);
  and and_14 (and_14_out, and_6_out, and_7_out);
  and and_15 (and_15_out, and_8_out, and_9_out);
  and and_16 (and_16_out, and_10_out, and_11_out);
  and and_17 (and_17_out, and_12_out, and_13_out);
  or or_3 (or_3_out, and_14_out, and_15_out);
  or or_4 (or_4_out, and_16_out, and_17_out);
  or or_5 (E, or_3_out, or_4_out);
  and and_18 (and_18_out, Q1, Q0);
  and and_19 (and_19_out, not_2_out, not_1_out);
  and and_20 (and_20_out, not_1_out, Q1);
  and and_21 (and_21_out, and_18_out, not_2_out);
  and and_22 (and_22_out, and_19_out, Q0);
  or or_6 (or_6_out, and_22_out, and_20_out);
  or or_7 (L, and_21_out, or_6_out);
endmodule
