// Logisim project Group -5,Problem-2(using basic gate).circ as structural Verilog: 1 circuit, main circuit main
module main (
  input  D,
  input  E,
  input  F,
  output B,
  output R
);

  wire and_1_out, and_2_out, and_3_out, not_1_out, or_1_out, xor_1_out;

  not not_1 (not_1_out, D);
  xor xor_1 (xor_1_out, D, E);
  xor xor_2 (R, xor_1_out, F);
  and and_1 (and_1_out, not_1_out, E);
  and and_2 (and_2_out, not_1_out, F);
  and and_3 (and_3_out, E, F);
  or or_1 (or_1_out, and_1_out, and_2_out);
  or or_2 (B, or_1_out, and_3_out);
endmodule
