// Logisim project Group_B2_05_Problem_02.circ as structural Verilog: 1 circuit, main circuit main
module main (
  input  D,
  input  E,
  input  F,
  output R,
  output B
);

  wire n7404_1_p2, n7408_1_p3, n7408_1_p6, n7408_1_p11, n7432_1_p3, n7486_1_p3;

  // _7404 7404_1: pin names not known; wires that end beside it: D, n7404_1_p2, 1'b0, 1'b1
  // _7486 7486_1: pin names not known; wires that end beside it: E, F, n7486_1_p3, 1'b0, 1'b1, n7486_1_p3, D, R
  // _7408 7408_1: pin names not known; wires that end beside it: E, F, n7408_1_p3, n7404_1_p2, E, n7408_1_p6, 1'b0, 1'b1, n7404_1_p2, F, n7408_1_p11
  // _7432 7432_1: pin names not known; wires that end beside it: n7408_1_p3, n7408_1_p6, n7432_1_p3, 1'b0, 1'b1, n7432_1_p3, n7408_1_p11, B
endmodule
