// Logisim project 4 bit universal shift register.circ as structural Verilog: 1 circuit, main circuit main
module main (
  input  Right_Shift,
  input  Left_Shift,
  input  S1,
  input  S0,
  input  I3,
  input  I2,
  input  I1,
  input  I0,
  output A3,
  output A2,
  output A1,
  output A0
);

  wire _4x1_MUX_2_p7, _4x1_MUX_2_p14, _4x1_MUX_p7, _4x1_MUX_p14, Clock_out, D_Flip_Flop_p1;

  // _74153 _4x1_MUX: pin names not known; wires that end beside it: 1'b0, S1, I3, A2, Right_Shift, A3, _4x1_MUX_p7, 1'b0, S0, I2, A1, A3, A2, _4x1_MUX_p14
  // _74153 _4x1_MUX_2: pin names not known; wires that end beside it: 1'b0, S1, I1, A0, A2, A1, _4x1_MUX_2_p7, 1'b0, S0, I0, Left_Shift, A1, A0, _4x1_MUX_2_p14
  Clock Clock (.out(Clock_out));
  // _7474 D_Flip_Flop: pin names not known; wires that end beside it: D_Flip_Flop_p1, _4x1_MUX_p7, Clock_out, A3, D_Flip_Flop_p1, _4x1_MUX_p14, Clock_out, A2
  // _7474 D_Flip_Flop_2: pin names not known; wires that end beside it: D_Flip_Flop_p1, _4x1_MUX_2_p7, Clock_out, A1, D_Flip_Flop_p1, _4x1_MUX_2_p14, Clock_out, A0
  Button Clear (.out(D_Flip_Flop_p1));
endmodule
