// Logisim project Offline_3_problem_1(using IC).circ as structural Verilog: 1 circuit, main circuit main
module main (
  input  J,
  input  K,
  output Qn,
  output Qn_prime
);

  wire CP_out, n7400_1_p3, n7400_1_p6, n7400_1_p9, n7400_2_p3, n7400_2_p6, n7400_2_p9, n7400_2_p12,
       n7400_3_p2, n7400_3_p3, n7400_3_p6, n7400_4_p6;

  Clock CP (.out(CP_out));
  // _7400 7400_1: pin names not known; wires that end beside it: J, CP_out, n7400_1_p3, n7400_1_p3, n7400_1_p3, n7400_1_p6, n7400_1_p6, Qn_prime, n7400_1_p9
  // _7400 7400_2: pin names not known; wires that end beside it: K, CP_out, n7400_2_p3, n7400_2_p3, n7400_2_p3, n7400_2_p6, n7400_2_p6, Qn, n7400_2_p9, CP_out, CP_out, n7400_2_p12
  // _7400 7400_3: pin names not known; wires that end beside it: n7400_1_p9, n7400_3_p2, n7400_3_p3, n7400_3_p3, n7400_2_p12, n7400_3_p6, n7400_3_p6, Qn_prime, Qn
  // _7400 7400_4: pin names not known; wires that end beside it: n7400_2_p9, n7400_3_p3, n7400_3_p2, n7400_3_p2, n7400_2_p12, n7400_4_p6, n7400_4_p6, Qn, Qn_prime

  // Notes on the sheet:
  //   1
  //   2
  //   9
  //   3
  //   4
  //   5
  //   7
  //   6
  //   8
endmodule
