// Logisim project Offline_3_problem_1(without IC).circ as structural Verilog: 1 circuit, main circuit main
module main (
  input  J,
  input  K,
  output Qn,
  output Qn_prime
);

  wire CP_out, nand_1_out, nand_2_out, nand_3_out, nand_4_out, nand_5_out, nand_6_out, nand_7_out,
       nand_8_out, nand_9_out, nand_10_out, nand_11_out;

  Clock CP (.out(CP_out));
  nand nand_1 (nand_1_out, J, CP_out);
  nand nand_2 (nand_2_out, CP_out, K);
  nand nand_3 (nand_3_out, nand_2_out, nand_2_out);
  nand nand_4 (nand_4_out, nand_1_out, nand_1_out);
  nand nand_5 (nand_5_out, Qn_prime, nand_4_out);
  nand nand_6 (nand_6_out, nand_3_out, Qn);
  nand nand_7 (nand_7_out, nand_5_out, nand_8_out);
  nand nand_8 (nand_8_out, nand_7_out, nand_6_out);
  nand nand_9 (nand_9_out, CP_out, CP_out);
  nand nand_10 (nand_10_out, nand_7_out, nand_9_out);
  nand nand_11 (nand_11_out, nand_8_out, nand_9_out);
  nand nand_12 (Qn, nand_10_out, Qn_prime);
  nand nand_13 (Qn_prime, Qn, nand_11_out);

  // Notes on the sheet:
  //   1
  //   2
  //   3
  //   4
  //   9
  //   5
  //   6
  //   7
  //   8
endmodule
