// Logisim project Universal shift register(without IC).circ as structural Verilog: 1 circuit, main circuit main
module main (
  input  R,
  input  L,
  input  [1:0] S1S0,
  input  I3,
  input  I2,
  input  I1,
  input  I0,
  output A3,
  output A2,
  output A1,
  output A0
);

  wire CLK_out, CLR_out, multiplexer_1_out, multiplexer_2_out, multiplexer_3_out, multiplexer_4_out;

  Multiplexer #(.select(2)) multiplexer_1 (
    .in0(A3), .in1(R), .in2(A2), .in3(I3), .out(multiplexer_1_out), .sel(S1S0));  // open: en
  Multiplexer #(.select(2)) multiplexer_2 (
    .in0(A2), .in1(A3), .in2(A1), .in3(I2), .out(multiplexer_2_out), .sel(S1S0));  // open: en
  Multiplexer #(.select(2)) multiplexer_3 (
    .in0(A1), .in1(A2), .in2(A0), .in3(I1), .out(multiplexer_3_out), .sel(S1S0));  // open: en
  Multiplexer #(.select(2)) multiplexer_4 (
    .in0(A0), .in1(A1), .in2(L), .in3(I0), .out(multiplexer_4_out), .sel(S1S0));  // open: en
  Clock CLK (.out(CLK_out));
  D_Flip_Flop d_ff_1 (.clk(CLK_out), .D(multiplexer_1_out), .Q(A3), .reset(CLR_out));  // open: Qn, preset, en
  D_Flip_Flop d_ff_2 (.clk(CLK_out), .D(multiplexer_2_out), .Q(A2), .reset(CLR_out));  // open: Qn, preset, en
  D_Flip_Flop d_ff_3 (.clk(CLK_out), .D(multiplexer_3_out), .Q(A1), .reset(CLR_out));  // open: Qn, preset, en
  D_Flip_Flop d_ff_4 (.clk(CLK_out), .D(multiplexer_4_out), .Q(A0), .reset(CLR_out));  // open: Qn, preset, en
  Button CLR (.out(CLR_out));
endmodule
