// Logisim project offline1.circ as structural Verilog: 1 circuit, main circuit main
module main (
  input  A4,
  input  A3,
  input  A2,
  input  A1,
  input  B4,
  input  B3,
  input  B2,
  input  B1,
  input  S2,
  input  S1,
  input  S0,
  output V,
  output Z,
  output S,
  output C,
  output S3,
  output S2_2,
  output S1_2,
  output Cout,
  output S4
);

  wire n7404_1_p3, n7408_1_p1, n7408_1_p2, n7408_1_p3, n7408_1_p6, n7408_1_p7, n7408_1_p9, n7408_1_p10,
       n7408_1_p12, n7408_2_p2, n7408_3_p2, n7408_3_p3, n7408_3_p6, n7408_3_p12, n7408_4_p2, n7408_4_p3,
       n7408_4_p5, n7408_4_p6, n7408_4_p7, n7408_4_p9, n7408_4_p10, n7432_1_p3, n7432_1_p5, n7432_1_p6,
       n7432_1_p7, n7432_1_p9, n7432_1_p12, n7432_2_p1, n7432_2_p6, n7486_1_p6, n7486_1_p9, n7486_1_p12;

  // _7408 7408_1: pin names not known; wires that end beside it: n7408_1_p1, n7408_1_p2, n7408_1_p3, n7408_1_p1, S2, n7408_1_p6, n7408_1_p7, S1, n7408_1_p9, n7408_1_p10, S1, n7408_1_p12
  // _7408 7408_2: pin names not known; wires that end beside it: n7408_1_p1, n7408_2_p2, V, n7408_1_p1, Cout, C
  // _7404 7404_1: pin names not known; wires that end beside it: S1, n7408_1_p1, n7404_1_p3, Z
  // _7486 7486_1: pin names not known; wires that end beside it: B1, S0, n7408_1_p7, B1, S1, n7486_1_p6, B2, S0, n7486_1_p9, B2, S1, n7486_1_p12
  // _7432 7432_1: pin names not known; wires that end beside it: n7408_1_p9, A1, n7432_1_p3, A3, n7432_1_p5, n7432_1_p6, n7432_1_p7, A2, n7432_1_p9, n7408_1_p12, A4, n7432_1_p12
  // _7486 7486_2: pin names not known; wires that end beside it: Cout, n7408_1_p2, n7408_2_p2
  // _7408 7408_3: pin names not known; wires that end beside it: n7408_1_p1, n7408_3_p2, n7408_3_p3, S0, n7486_1_p6, n7408_3_p6, S1, n7486_1_p9, n7432_1_p7, n7486_1_p12, S0, n7408_3_p12
  // _7408 7408_4: pin names not known; wires that end beside it: n7408_1_p1, n7408_4_p2, n7408_4_p3, S0, n7408_4_p5, n7408_4_p6, n7408_4_p7, S0, n7408_4_p9, n7408_4_p10, S1, n7432_1_p5
  // _7486 7486_3: pin names not known; wires that end beside it: B3, S1, n7408_4_p7, B3, S0, n7408_4_p10, S1, B4, n7408_4_p5, B4, S0, n7408_1_p10
  // _7432 7432_2: pin names not known; wires that end beside it: n7432_2_p1, S, n7404_1_p3, S1_2, S2_2, n7432_2_p6, n7432_2_p6, S3, n7432_2_p1, 1'b0
  // _7483 ADDER_2: pin names not known; wires that end beside it: 1'b0, S3, 1'b0, n7432_1_p6, n7408_1_p2, n7408_4_p9, 1'b1, 1'b0, n7408_1_p3, n7408_4_p3, 1'b1, Cout, S, n7432_1_p12, n7408_4_p6
  // _7483 ADDER_1: pin names not known; wires that end beside it: 1'b0, S1_2, 1'b0, n7432_1_p3, n7408_3_p2, n7408_3_p6, 1'b1, 1'b0, n7408_3_p3, n7408_1_p6, 1'b1, n7408_4_p2, S2_2, n7432_1_p9, n7408_3_p12

  assign S4 = S;

  // Notes on the sheet:
  //   Cin or C1
  //   Control Bit
  //   Function Bit
  //   Z4
  //   Z1
  //   X3
  //   X1
  //   X2
  //   C2
  //   C3
  //   Z3
  //   Z2
  //   Y1
  //   Y3
  //   C4
  //   Y2
  //   Y4
  //   X4
  //   Y4
  //   Y3
  //   X4
  //   Z4
  //   C4
  //   X3
  //   Z3
  //   Y2
  //   C3
  //   Z2
  //   X2
  //   X1
  //   Y1
  //   C2
  //   Cin
  //   GROUND
endmodule
