// Logisim project Offline_2.circ as structural Verilog: 9 circuits, main circuit main
module main (
  input  [31:0] A,
  input  [31:0] B,
  output [23:0] Smaller_Significant,
  output [4:0] Difference_in_Exponent,
  output [23:0] Larger_Significant,
  output [9:0] Larger_Exponent,
  output [23:0] out_7,
  output [23:0] out_8
);

  wire comparator_1_x__y, comparator_1_x_y;
  wire [23:0] shifter_1_out, sign_adjustment_1_out_3, sign_adjustment_2_out_3;

  Comparator comparator_1 (
    .X(A[30:21]), .Y(B[30:21]), .X__Y(comparator_1_x__y), .X_Y(comparator_1_x_y),
    .Difference(Difference_in_Exponent), .Larger(Larger_Exponent));  // open: out_5
  Sign_Adjustment sign_adjustment_1 (.in_1({3'b001, A[20:0]}), .Sign_Bit(A[31]), .out_3(sign_adjustment_1_out_3));
  _24_Bit_Mux_Module MUX (
    .Selection_But(comparator_1_x__y), .A(sign_adjustment_1_out_3), .B(sign_adjustment_2_out_3),
    .Output(Smaller_Significant));
  Shifter #(.width(24), .shift("ar")) shifter_1 (
    .in(Smaller_Significant), .\dist (Difference_in_Exponent), .out(shifter_1_out));
  Adder #(.width(24)) adder_1 (.a(shifter_1_out), .b(Larger_Significant), .out(out_7), .cin(1'b0));  // open: cout
  Complementing_result complementing_result_1 (.Input(out_7), .Output(out_8));  // open: out_3
  _24_Bit_Mux_Module MUX_2 (
    .Selection_But(comparator_1_x_y), .A(sign_adjustment_1_out_3), .B(sign_adjustment_2_out_3),
    .Output(Larger_Significant));
  Sign_Adjustment sign_adjustment_2 (.in_1({3'b001, B[20:0]}), .Sign_Bit(B[31]), .out_3(sign_adjustment_2_out_3));

  // Notes on the sheet:
  //   Adjusting sign
  //   Arethmetic right shift or logical ?
  //   Complementing result
  //   Adjusting sign
endmodule

module Comparator (
  input  [9:0] X,
  input  [9:0] Y,
  output X__Y,
  output X_Y,
  output out_5,
  output [4:0] Difference,
  output [9:0] Larger
);

  wire comparator_1_eq, comparator_1_gt;
  wire [9:0] n10_bit_mux_module_2_output;
  wire [9:5] subtractor_1_out;

  Comparator_part #(.width(10)) comparator_1 (.a(X), .b(Y), .gt(comparator_1_gt), .eq(comparator_1_eq), .lt(X_Y));
  // _7432 7432_1: pin names not known; wires that end beside it: comparator_1_gt, comparator_1_eq, X__Y
  _10_Bit_Mux_Module u_10_bit_mux_module_1 (.SELECTION(X_Y), .A(X), .B(Y), .\output (Larger));
  _10_Bit_Mux_Module u_10_bit_mux_module_2 (.SELECTION(X__Y), .A(X), .B(Y), .\output (n10_bit_mux_module_2_output));
  Subtractor #(.width(10)) subtractor_1 (
    .a(Larger), .b(n10_bit_mux_module_2_output), .out({subtractor_1_out, Difference}), .bin(1'b0),
    .bout(out_5));

  // Notes on the sheet:
  //   Exponent of A
  //   Exponent of B
  //   Larger
  //   Smaller
  //   jehetu 32 bit er beshi shift kora possible na?
endmodule

module Sign_Adjustment (
  input  [23:0] in_1,
  input  Sign_Bit,
  output [23:0] out_3
);

  wire [23:0] negator_1_out;

  Negator #(.width(24)) negator_1 (.in(in_1), .out(negator_1_out));
  _24_Bit_Mux_Module u_24_bit_mux_module_1 (.Selection_But(Sign_Bit), .A(in_1), .B(negator_1_out), .Output(out_3));
endmodule

module Complementing_result (
  input  [23:0] Input,
  output [23:0] Output,
  output out_3
);

  wire [23:0] negator_1_out;

  Negator #(.width(24)) negator_1 (.in(Input), .out(negator_1_out));
  _24_Bit_Mux_Module u_24_bit_mux_module_1 (.Selection_But(Input[23]), .A(Input), .B(negator_1_out), .Output(Output));

  assign out_3 = Input[23];
endmodule

module _4_Bit_Mux_Module (
  input  A0,
  input  A1,
  input  A2,
  input  A3,
  input  B0,
  input  B1,
  input  B2,
  input  B3,
  input  SELECTION,
  output _0,
  output _1,
  output _2,
  output _3
);

  // _74157 74157_1: pin names not known; wires that end beside it: SELECTION, A0, B0, _0, A1, B1, _1, 1'b0, 1'b1, 1'b0, A3, B3, _3, A2, B2, _2
endmodule

module _2_bit_Mux_Module (
  input  A0,
  input  A1,
  input  B0,
  input  B1,
  input  SELECTION,
  output out_6,
  output out_7
);

  // _74157 74157_1: pin names not known; wires that end beside it: SELECTION, A0, B0, out_6, A1, B1, out_7, 1'b0, 1'b1, 1'b0
endmodule

// MUX
module _10_Bit_Mux_Module (
  input  [9:0] B,
  input  SELECTION,
  input  [9:0] A,
  output [9:0] \output 
);

  _4_Bit_Mux_Module u_4_bit_mux_module_1 (
    .SELECTION(SELECTION), .A0(A[0]), .A1(A[1]), .A2(A[2]), .A3(A[3]), .B0(B[0]), .B1(B[1]), .B2(B[2]),
    .B3(B[3]), ._0(\output [0]), ._1(\output [1]), ._2(\output [2]), ._3(\output [3]));
  _4_Bit_Mux_Module u_4_bit_mux_module_2 (
    .SELECTION(SELECTION), .A0(A[4]), .A1(A[5]), .A2(A[6]), .A3(A[7]), .B0(B[4]), .B1(B[5]), .B2(B[6]),
    .B3(B[7]), ._0(\output [4]), ._1(\output [5]), ._2(\output [6]), ._3(\output [7]));
  _2_bit_Mux_Module u_2_bit_mux_module_1 (
    .SELECTION(SELECTION), .A0(A[8]), .A1(A[9]), .B0(B[8]), .B1(B[9]), .out_6(\output [8]),
    .out_7(\output [9]));

  // Notes on the sheet:
  //   A
endmodule

module _23_Bit_Mux_Module (
  input  [21:0] B,
  input  [21:0] A,
  input  Selection,
  output _4,
  output _5,
  output _6,
  output _7,
  output _0,
  output _1,
  output _2,
  output _8,
  output _9,
  output _10,
  output _11,
  output _12,
  output _13,
  output _14,
  output _15,
  output _16,
  output _17,
  output _18,
  output _19,
  output _20,
  output _21,
  output _3
);

  _4_Bit_Mux_Module u_4_bit_mux_module_1 (
    .SELECTION(Selection), .A0(A[0]), .A1(A[1]), .A2(A[2]), .A3(A[3]), .B0(B[0]), .B1(B[1]), .B2(B[2]),
    .B3(B[3]), ._0(_0), ._1(_1), ._2(_2), ._3(_3));
  _4_Bit_Mux_Module u_4_bit_mux_module_2 (
    .SELECTION(Selection), .A0(A[4]), .A1(A[5]), .A2(A[6]), .A3(A[7]), .B0(B[4]), .B1(B[5]), .B2(B[6]),
    .B3(B[7]), ._0(_4), ._1(_5), ._2(_6), ._3(_7));
  _4_Bit_Mux_Module u_4_bit_mux_module_3 (
    .SELECTION(Selection), .A0(A[8]), .A1(A[9]), .A2(A[10]), .A3(A[11]), .B0(B[8]), .B1(B[9]), .B2(B[10]),
    .B3(B[11]), ._0(_8), ._1(_9), ._2(_10), ._3(_11));
  _4_Bit_Mux_Module u_4_bit_mux_module_4 (
    .SELECTION(Selection), .A0(A[12]), .A1(A[13]), .A2(A[14]), .A3(A[15]), .B0(B[12]), .B1(B[13]),
    .B2(B[14]), .B3(B[15]), ._0(_12), ._1(_13), ._2(_14), ._3(_15));
  _4_Bit_Mux_Module u_4_bit_mux_module_5 (
    .SELECTION(Selection), .A0(A[16]), .A1(A[17]), .A2(A[18]), .A3(A[19]), .B0(B[16]), .B1(B[17]),
    .B2(B[18]), .B3(B[19]), ._0(_16), ._1(_17), ._2(_18), ._3(_19));
  _2_bit_Mux_Module u_2_bit_mux_module_1 (
    .SELECTION(Selection), .A0(A[20]), .A1(A[21]), .B0(B[20]), .B1(B[21]), .out_6(_20), .out_7(_21));
endmodule

// S
module _24_Bit_Mux_Module (
  input  [23:0] B,
  input  Selection_But,
  input  [23:0] A,
  output [23:0] Output
);

  _4_Bit_Mux_Module u_4_bit_mux_module_1 (
    .SELECTION(Selection_But), .A0(A[0]), .A1(A[1]), .A2(A[2]), .A3(A[3]), .B0(B[0]), .B1(B[1]), .B2(B[2]),
    .B3(B[3]), ._0(Output[0]), ._1(Output[1]), ._2(Output[2]), ._3(Output[3]));
  _4_Bit_Mux_Module u_4_bit_mux_module_2 (
    .SELECTION(Selection_But), .A0(A[4]), .A1(A[5]), .A2(A[6]), .A3(A[7]), .B0(B[4]), .B1(B[5]), .B2(B[6]),
    .B3(B[7]), ._0(Output[4]), ._1(Output[5]), ._2(Output[6]), ._3(Output[7]));
  _4_Bit_Mux_Module u_4_bit_mux_module_3 (
    .SELECTION(Selection_But), .A0(A[8]), .A1(A[9]), .A2(A[10]), .A3(A[11]), .B0(B[8]), .B1(B[9]),
    .B2(B[10]), .B3(B[11]), ._0(Output[8]), ._1(Output[9]), ._2(Output[10]), ._3(Output[11]));
  _4_Bit_Mux_Module u_4_bit_mux_module_4 (
    .SELECTION(Selection_But), .A0(A[12]), .A1(A[13]), .A2(A[14]), .A3(A[15]), .B0(B[12]), .B1(B[13]),
    .B2(B[14]), .B3(B[15]), ._0(Output[12]), ._1(Output[13]), ._2(Output[14]), ._3(Output[15]));
  _4_Bit_Mux_Module u_4_bit_mux_module_5 (
    .SELECTION(Selection_But), .A0(A[16]), .A1(A[17]), .A2(A[18]), .A3(A[19]), .B0(B[16]), .B1(B[17]),
    .B2(B[18]), .B3(B[19]), ._0(Output[16]), ._1(Output[17]), ._2(Output[18]), ._3(Output[19]));
  _4_Bit_Mux_Module u_4_bit_mux_module_6 (
    .SELECTION(Selection_But), .A0(A[20]), .A1(A[21]), .A2(A[22]), .A3(A[23]), .B0(B[20]), .B1(B[21]),
    .B2(B[22]), .B3(B[23]), ._0(Output[20]), ._1(Output[21]), ._2(Output[22]), ._3(Output[23]));
endmodule
