// Logisim project Offline_2_dev_version-2.5.circ as structural Verilog: 12 circuits, main circuit main
module main (
  input  [31:0] A,
  input  [31:0] B,
  output [23:0] Smaller_Significant,
  output [4:0] Difference_in_Exponent,
  output [23:0] Larger_Significant,
  output [9:0] Larger_Exponent,
  output [23:0] out_7,
  output Sign_Bit_store_kora_lagbe_na,
  output [23:0] out_9
);

  wire comparator_1_x__y, comparator_1_x_y;
  wire [23:0] shifter_1_out, sign_adjustment_1_out_3, sign_adjustment_2_out_3;

  Comparator comparator_1 (
    .X(A[30:21]), .Y(B[30:21]), .X__Y(comparator_1_x__y), .X_Y(comparator_1_x_y),
    .Difference(Difference_in_Exponent), .Larger(Larger_Exponent));  // open: out_5
  Sign_Adjustment sign_adjustment_1 (.in_1({3'b001, A[20:0]}), .Sign_Bit(A[31]), .out_3(sign_adjustment_1_out_3));
  Multiplexer #(.width(24), .enable("false")) multiplexer_1 (
    .in0(sign_adjustment_1_out_3), .in1(sign_adjustment_2_out_3), .out(Smaller_Significant),
    .sel(comparator_1_x__y));
  Shifter #(.width(24), .shift("ar")) shifter_1 (
    .in(Smaller_Significant), .\dist (Difference_in_Exponent), .out(shifter_1_out));
  Adder #(.width(24)) adder_1 (.a(shifter_1_out), .b(Larger_Significant), .out(out_7), .cin(1'b0));  // open: cout
  Complementing_result complementing_result_1 (.Input(out_7), .Output(out_9), .out_3(Sign_Bit_store_kora_lagbe_na));
  Multiplexer #(.width(24), .enable("false")) multiplexer_2 (
    .in0(sign_adjustment_1_out_3), .in1(sign_adjustment_2_out_3), .out(Larger_Significant),
    .sel(comparator_1_x_y));
  Sign_Adjustment sign_adjustment_2 (.in_1({3'b001, B[20:0]}), .Sign_Bit(B[31]), .out_3(sign_adjustment_2_out_3));

  // Notes on the sheet:
  //   Adjusting sign
  //   Arethmetic right shift or logical ?
  //   Complementing result
  //   Adjusting sign
endmodule

module Comparator (
  input  [9:0] X,
  input  [9:0] Y,
  output X__Y,
  output X_Y,
  output out_5,
  output [4:0] Difference,
  output [9:0] Larger
);

  wire comparator_1_eq, comparator_1_gt;
  wire [9:0] n10_bit_mux_module_2_output;
  wire [9:5] subtractor_1_out;

  Comparator_part #(.width(10)) comparator_1 (.a(X), .b(Y), .gt(comparator_1_gt), .eq(comparator_1_eq), .lt(X_Y));
  // _7432 7432_1: pin names not known; wires that end beside it: comparator_1_gt, comparator_1_eq, X__Y
  _10_Bit_Mux_Module u_10_bit_mux_module_1 (.SELECTION(X_Y), .A(X), .B(Y), .\output (Larger));
  _10_Bit_Mux_Module u_10_bit_mux_module_2 (.SELECTION(X__Y), .A(X), .B(Y), .\output (n10_bit_mux_module_2_output));
  Subtractor #(.width(10)) subtractor_1 (
    .a(Larger), .b(n10_bit_mux_module_2_output), .out({subtractor_1_out, Difference}), .bin(1'b0),
    .bout(out_5));

  // Notes on the sheet:
  //   Exponent of A
  //   Exponent of B
  //   Larger
  //   Smaller
  //   jehetu 32 bit er beshi shift kora possible na?
endmodule

module Sign_Adjustment (
  input  [23:0] in_1,
  input  Sign_Bit,
  output [23:0] out_3
);

  wire [23:0] negator_1_out;

  Negator #(.width(24)) negator_1 (.in(in_1), .out(negator_1_out));
  Multiplexer #(.width(24), .enable("false")) multiplexer_1 (
    .in0(in_1), .in1(negator_1_out), .out(out_3), .sel(Sign_Bit));
endmodule

module Complementing_result (
  input  [23:0] Input,
  output [23:0] Output,
  output out_3
);

  wire [23:0] negator_1_out;

  Negator #(.width(24)) negator_1 (.in(Input), .out(negator_1_out));
  Multiplexer #(.width(24), .enable("false")) multiplexer_1 (
    .in0(Input), .in1(negator_1_out), .out(Output), .sel(Input[23]));

  assign out_3 = Input[23];
endmodule

module _4_Bit_Mux_Module (
  input  A0,
  input  A1,
  input  A2,
  input  A3,
  input  B0,
  input  B1,
  input  B2,
  input  B3,
  input  SELECTION,
  output _0,
  output _1,
  output _2,
  output _3
);

  // _74157 74157_1: pin names not known; wires that end beside it: SELECTION, A0, B0, _0, A1, B1, _1, 1'b0, 1'b1, 1'b0, A3, B3, _3, A2, B2, _2
endmodule

module _2_bit_Mux_Module (
  input  A0,
  input  A1,
  input  B0,
  input  B1,
  input  SELECTION,
  output out_6,
  output out_7
);

  // _74157 74157_1: pin names not known; wires that end beside it: SELECTION, A0, B0, out_6, A1, B1, out_7, 1'b0, 1'b1, 1'b0
endmodule

// MUX
module _10_Bit_Mux_Module (
  input  [9:0] B,
  input  SELECTION,
  input  [9:0] A,
  output [9:0] \output 
);

  _4_Bit_Mux_Module u_4_bit_mux_module_1 (
    .SELECTION(SELECTION), .A0(A[0]), .A1(A[1]), .A2(A[2]), .A3(A[3]), .B0(B[0]), .B1(B[1]), .B2(B[2]),
    .B3(B[3]), ._0(\output [0]), ._1(\output [1]), ._2(\output [2]), ._3(\output [3]));
  _4_Bit_Mux_Module u_4_bit_mux_module_2 (
    .SELECTION(SELECTION), .A0(A[4]), .A1(A[5]), .A2(A[6]), .A3(A[7]), .B0(B[4]), .B1(B[5]), .B2(B[6]),
    .B3(B[7]), ._0(\output [4]), ._1(\output [5]), ._2(\output [6]), ._3(\output [7]));
  _2_bit_Mux_Module u_2_bit_mux_module_1 (
    .SELECTION(SELECTION), .A0(A[8]), .A1(A[9]), .B0(B[8]), .B1(B[9]), .out_6(\output [8]),
    .out_7(\output [9]));

  // Notes on the sheet:
  //   A
endmodule

module _23_Bit_Mux_Module (
  input  [21:0] B,
  input  [21:0] A,
  input  Selection,
  output _4,
  output _5,
  output _6,
  output _7,
  output _0,
  output _1,
  output _2,
  output _8,
  output _9,
  output _10,
  output _11,
  output _12,
  output _13,
  output _14,
  output _15,
  output _16,
  output _17,
  output _18,
  output _19,
  output _20,
  output _21,
  output _3
);

  _4_Bit_Mux_Module u_4_bit_mux_module_1 (
    .SELECTION(Selection), .A0(A[0]), .A1(A[1]), .A2(A[2]), .A3(A[3]), .B0(B[0]), .B1(B[1]), .B2(B[2]),
    .B3(B[3]), ._0(_0), ._1(_1), ._2(_2), ._3(_3));
  _4_Bit_Mux_Module u_4_bit_mux_module_2 (
    .SELECTION(Selection), .A0(A[4]), .A1(A[5]), .A2(A[6]), .A3(A[7]), .B0(B[4]), .B1(B[5]), .B2(B[6]),
    .B3(B[7]), ._0(_4), ._1(_5), ._2(_6), ._3(_7));
  _4_Bit_Mux_Module u_4_bit_mux_module_3 (
    .SELECTION(Selection), .A0(A[8]), .A1(A[9]), .A2(A[10]), .A3(A[11]), .B0(B[8]), .B1(B[9]), .B2(B[10]),
    .B3(B[11]), ._0(_8), ._1(_9), ._2(_10), ._3(_11));
  _4_Bit_Mux_Module u_4_bit_mux_module_4 (
    .SELECTION(Selection), .A0(A[12]), .A1(A[13]), .A2(A[14]), .A3(A[15]), .B0(B[12]), .B1(B[13]),
    .B2(B[14]), .B3(B[15]), ._0(_12), ._1(_13), ._2(_14), ._3(_15));
  _4_Bit_Mux_Module u_4_bit_mux_module_5 (
    .SELECTION(Selection), .A0(A[16]), .A1(A[17]), .A2(A[18]), .A3(A[19]), .B0(B[16]), .B1(B[17]),
    .B2(B[18]), .B3(B[19]), ._0(_16), ._1(_17), ._2(_18), ._3(_19));
  _2_bit_Mux_Module u_2_bit_mux_module_1 (
    .SELECTION(Selection), .A0(A[20]), .A1(A[21]), .B0(B[20]), .B1(B[21]), .out_6(_20), .out_7(_21));
endmodule

module Normalizer (
  input  [31:0] Input,
  input  [10:0] Larger_Exponent,
  output [20:0] Final_21_bit_Fraction_Output,
  output [4:0] Shift_Amount,
  output All_0s,
  output [31:0] input_for_rounding,
  output b_out,
  output [9:0] Exponent_After_Normalization,
  output To_detect_negative,
  output Sign_Bit_of_Exponent
);

  wire bitfinder_1_found;
  wire [10:0] subtractor_1_out;
  wire [31:0] shifter_1_out;

  Subtractor #(.width(11)) subtractor_1 (
    .a({{6{1'b0}}, Shift_Amount}), .b(11'h2), .out(subtractor_1_out), .bin(1'b0), .bout(To_detect_negative));
  BitFinder #(.width(32)) bitfinder_1 (.in({Input[31:1], 1'b0}), .index(Shift_Amount), .found(bitfinder_1_found));
  Shifter #(.width(32)) shifter_1 (
    .in(Input), .\dist (Shift_Amount),
    .out({shifter_1_out[31], Final_21_bit_Fraction_Output, input_for_rounding[7:0], shifter_1_out[1:0]}));
  // _7404 NOTGate__IC: pin names not known; wires that end beside it: bitfinder_1_found, All_0s
  Subtractor #(.width(11)) subtractor_2 (
    .a(Larger_Exponent), .b(subtractor_1_out), .out({Sign_Bit_of_Exponent, Exponent_After_Normalization}),
    .bin(1'b0), .bout(b_out));

  assign input_for_rounding[31:8] = {3'b001, Final_21_bit_Fraction_Output};

  // Notes on the sheet:
  //   Shift Amount of Normalization
  //   Shift amount in 10 bits
  //   Shifter
  //   Significand 1
endmodule

module Overflow_or_Underflow (
  input  [9:0] Exponent_bits_after_normalization,
  input  Fraction_All_0s_or_not,
  input  Sign_Bit_of_Exponent_From_Normalization,
  output Overflow,
  output Underflow
);

  wire bitfinder_1_found, bitfinder_2_found, n7404_1_p2, n7404_1_p4, n7408_1_p3;

  BitFinder #(.width(10), .\type ("low0")) bitfinder_1 (
    .in(Exponent_bits_after_normalization), .found(bitfinder_1_found));  // open: index
  BitFinder #(.width(10)) bitfinder_2 (
    .in(Exponent_bits_after_normalization), .found(bitfinder_2_found));  // open: index
  // _7404 7404_1: pin names not known; wires that end beside it: bitfinder_2_found, n7404_1_p2, Fraction_All_0s_or_not, n7404_1_p4, bitfinder_1_found, Overflow
  // _7408 7408_1: pin names not known; wires that end beside it: n7404_1_p2, n7404_1_p4, n7408_1_p3
  // _7432 7432_1: pin names not known; wires that end beside it: n7408_1_p3, Sign_Bit_of_Exponent_From_Normalization, Underflow
endmodule

module _32_bit_Mux_Module (
  input  [31:0] Input_0,
  input  [31:0] Input_1,
  input  Selection,
  output [31:0] Output
);

  _16_bit_Mux_Module u_16_bit_mux_module_1 (
    .Selection(Selection), .Input_0(Input_0[15:0]), .Output(Output[15:0]), .Input_1(Input_1[15:0]));
  _16_bit_Mux_Module u_16_bit_mux_module_2 (
    .Selection(Selection), .Input_0(Input_0[31:16]), .Output(Output[31:16]), .Input_1(Input_1[31:16]));
endmodule

module _16_bit_Mux_Module (
  input  [15:0] Input_1,
  input  Selection,
  input  [15:0] Input_0,
  output [15:0] Output
);

  _4_Bit_Mux_Module u_4_bit_mux_module_1 (
    .SELECTION(Selection), .A0(Input_0[0]), .A1(Input_0[1]), .A2(Input_0[2]), .A3(Input_0[3]),
    .B0(Input_1[0]), .B1(Input_1[1]), .B2(Input_1[2]), .B3(Input_1[3]), ._0(Output[0]), ._1(Output[1]),
    ._2(Output[2]), ._3(Output[3]));
  _4_Bit_Mux_Module u_4_bit_mux_module_2 (
    .SELECTION(Selection), .A0(Input_0[4]), .A1(Input_0[5]), .A2(Input_0[6]), .A3(Input_0[7]),
    .B0(Input_1[4]), .B1(Input_1[5]), .B2(Input_1[6]), .B3(Input_1[7]), ._0(Output[4]), ._1(Output[5]),
    ._2(Output[6]), ._3(Output[7]));
  _4_Bit_Mux_Module u_4_bit_mux_module_3 (
    .SELECTION(Selection), .A0(Input_0[8]), .A1(Input_0[9]), .A2(Input_0[10]), .A3(Input_0[11]),
    .B0(Input_1[8]), .B1(Input_1[9]), .B2(Input_1[10]), .B3(Input_1[11]), ._0(Output[8]), ._1(Output[9]),
    ._2(Output[10]), ._3(Output[11]));
  _4_Bit_Mux_Module u_4_bit_mux_module_4 (
    .SELECTION(Selection), .A0(Input_0[12]), .A1(Input_0[13]), .A2(Input_0[14]), .A3(Input_0[15]),
    .B0(Input_1[12]), .B1(Input_1[13]), .B2(Input_1[14]), .B3(Input_1[15]), ._0(Output[12]), ._1(Output[13]),
    ._2(Output[14]), ._3(Output[15]));
endmodule
