// Logisim project Offline_2_version_5-1.circ as structural Verilog: 8 circuits, main circuit main
// Main Adder
module main (
  input  [31:0] A,
  input  [31:0] B,
  input  [31:0] Spectal_case_of_All_zero_output,
  output [31:0] Smaller_Exponent_Significant,
  output [4:0] Difference_in_Exponent,
  output [31:0] Larger_Exponent_Significant,
  output [9:0] Larger_Exponent,
  output [31:0] out_8,
  output Storing_output_Sign_Bit,
  output [31:0] out_10,
  output [20:0] Output_fraction_after_1str_normalization,
  output [9:0] Exponent_after_1st_normalization,
  output OF_after_1st_NRM,
  output UF_after_1st_NRM,
  output [20:0] Output_fraction_after_2nd_normalization,
  output [9:0] Exponent_after_2nd_normalization,
  output OF_after_2nd_NRM,
  output UF_after_2nd_NRM,
  output [31:0] Result,
  output Underflow,
  output Overflow
);

  wire Exponent_Comparator_x__y, Exponent_Comparator_x_y, n7432_1_p3, normalizer_1_all_0s,
       normalizer_1_sign_bit_of_exponent, normalizer_2_all_0s, normalizer_2_sign_bit_of_exponent;
  wire [31:0] n32_bit_mux_module_1_output, normalizer_1_input_for_rounding, rounding_1_output, shifter_1_out,
       sign_adjustment_1_out_3, sign_adjustment_2_out_3;

  Comparator Exponent_Comparator (
    .X(A[30:21]), .Y(B[30:21]), .X__Y(Exponent_Comparator_x__y), .X_Y(Exponent_Comparator_x_y),
    .Difference(Difference_in_Exponent), .Larger(Larger_Exponent));  // open: out_5
  Sign_Adjustment sign_adjustment_1 (
    .in_1({3'b001, A[20:0], {8{1'b0}}}), .Sign_Bit(A[31]), .out_3(sign_adjustment_1_out_3));
  _32_bit_Mux_Module _32_bit_MUX (
    .Input_0(sign_adjustment_1_out_3), .Input_1(sign_adjustment_2_out_3),
    .Selection(Exponent_Comparator_x__y), .Output(Smaller_Exponent_Significant));
  _32_bit_Mux_Module u_32_bit_mux_module_1 (
    .Input_0({Storing_output_Sign_Bit, Exponent_after_2nd_normalization, Output_fraction_after_2nd_normalization}),
    .Input_1({Storing_output_Sign_Bit, Exponent_after_1st_normalization, Output_fraction_after_1str_normalization}),
    .Selection(n7432_1_p3), .Output(n32_bit_mux_module_1_output));
  Shifter #(.width(32), .shift("ar")) shifter_1 (
    .in(Smaller_Exponent_Significant), .\dist (Difference_in_Exponent), .out(shifter_1_out));
  _32_bit_Mux_Module u_32_bit_mux_module_2 (
    .Input_0(n32_bit_mux_module_1_output), .Input_1(Spectal_case_of_All_zero_output),
    .Selection(normalizer_1_all_0s), .Output(Result));
  Adder #(.width(32)) adder_1 (
    .a(shifter_1_out), .b(Larger_Exponent_Significant), .out(out_8), .cin(1'b0));  // open: cout
  _32_bit_Mux_Module _32_Bit_MUX_2 (
    .Input_0(sign_adjustment_1_out_3), .Input_1(sign_adjustment_2_out_3),
    .Selection(Exponent_Comparator_x_y), .Output(Larger_Exponent_Significant));
  Complementing_result complementing_result_1 (.Input(out_8), .Output(out_10), .out_3(Storing_output_Sign_Bit));
  Overflow_or_Underflow overflow_or_underflow_1 (
    .Exponent_bits_after_normalization(Exponent_after_1st_normalization),
    .Fraction_All_0s_or_not(normalizer_1_all_0s),
    .Sign_Bit_of_Exponent_From_Normalization(normalizer_1_sign_bit_of_exponent), .Overflow(OF_after_1st_NRM),
    .Underflow(UF_after_1st_NRM));
  Normalizer normalizer_1 (
    .Input(out_10), .Larger_Exponent({1'b0, Larger_Exponent}),
    .Final_21_bit_Fraction_Output(Output_fraction_after_1str_normalization), .All_0s(normalizer_1_all_0s),
    .input_for_rounding(normalizer_1_input_for_rounding),
    .Exponent_After_Normalization(Exponent_after_1st_normalization),
    .Sign_Bit_of_Exponent(normalizer_1_sign_bit_of_exponent));  // open: Shift_Amount, b_out, To_detect_negative
  // _7432 7432_1: pin names not known; wires that end beside it: OF_after_1st_NRM, UF_after_1st_NRM, n7432_1_p3
  Sign_Adjustment sign_adjustment_2 (
    .in_1({3'b001, B[20:0], {8{1'b0}}}), .Sign_Bit(B[31]), .out_3(sign_adjustment_2_out_3));
  Rounding rounding_1 (.\input (normalizer_1_input_for_rounding), .\output (rounding_1_output));
  // _74157 74157_1: pin names not known; wires that end beside it: n7432_1_p3, UF_after_2nd_NRM, UF_after_1st_NRM, Underflow, OF_after_2nd_NRM, OF_after_1st_NRM, Overflow, 1'b0
  Normalizer normalizer_2 (
    .Input(rounding_1_output), .Larger_Exponent({1'b0, Exponent_after_1st_normalization}),
    .Final_21_bit_Fraction_Output(Output_fraction_after_2nd_normalization), .All_0s(normalizer_2_all_0s),
    .Exponent_After_Normalization(Exponent_after_2nd_normalization),
    .Sign_Bit_of_Exponent(normalizer_2_sign_bit_of_exponent));  // open: Shift_Amount, input_for_rounding, b_out, To_detect_negative
  Overflow_or_Underflow overflow_or_underflow_2 (
    .Exponent_bits_after_normalization(Exponent_after_2nd_normalization),
    .Fraction_All_0s_or_not(normalizer_2_all_0s),
    .Sign_Bit_of_Exponent_From_Normalization(normalizer_2_sign_bit_of_exponent), .Overflow(OF_after_2nd_NRM),
    .Underflow(UF_after_2nd_NRM));

  // Notes on the sheet:
  //   Output after 1st normalization (if overflow or underflow occurs)
  //   Adjusting sign
  //   Arethmetic right shift 
  //   this MUX is for handling special case of All zeros
  //   For 1st Overflow and underflow
  //   Output after 2nd normalization
  //   Complementing result
  //   Result of significand addition
  //   1st Normalizer
  //   Adjusting sign
  //   Rounder
  //   2nd Normalizer
  //   For 2nd Overflow and underflow
  //   MUX for selecting correct OF and UF
endmodule

module Comparator (
  input  [9:0] X,
  input  [9:0] Y,
  output X__Y,
  output X_Y,
  output out_5,
  output [4:0] Difference,
  output [9:0] Larger
);

  wire comparator_1_eq, comparator_1_gt, comparator_2_gt;
  wire [4:0] subtractor_1_out_2;
  wire [9:0] n10_bit_mux_module_2_output;
  wire [9:5] subtractor_1_out;

  Comparator_part #(.width(10), .mode("unsigned")) comparator_1 (
    .a(X), .b(Y), .gt(comparator_1_gt), .eq(comparator_1_eq), .lt(X_Y));
  // _7432 7432_1: pin names not known; wires that end beside it: comparator_1_gt, comparator_1_eq, X__Y
  _10_Bit_Mux_Module u_10_bit_mux_module_1 (.SELECTION(X_Y), .A(X), .B(Y), .\output (Larger));
  _10_Bit_Mux_Module u_10_bit_mux_module_2 (.SELECTION(X__Y), .A(X), .B(Y), .\output (n10_bit_mux_module_2_output));
  Subtractor #(.width(10)) subtractor_1 (
    .a(Larger), .b(n10_bit_mux_module_2_output), .out({subtractor_1_out, subtractor_1_out_2}), .bin(1'b0),
    .bout(out_5));
  Comparator_part #(.width(10), .mode("unsigned")) comparator_2 (
    .a(10'h1f), .b({subtractor_1_out, subtractor_1_out_2}), .gt(comparator_2_gt));  // open: eq, lt
  Multiplexer #(.width(5), .enable("false")) multiplexer_1 (
    .in0({5{1'b1}}), .in1(subtractor_1_out_2), .out(Difference), .sel(comparator_2_gt));

  // Notes on the sheet:
  //   Exponent of A
  //   Exponent of B
  //   Larger
  //   Smaller
  //   0000011111
  //   32 > diff hoile diff jacche, r naile 32 hacche
endmodule

module Sign_Adjustment (
  input  [31:0] in_1,
  input  Sign_Bit,
  output [31:0] out_3
);

  wire [31:0] negator_1_out;

  Negator #(.width(32)) negator_1 (.in(in_1), .out(negator_1_out));
  _32_bit_Mux_Module u_32_bit_mux_module_1 (
    .Input_0(in_1), .Input_1(negator_1_out), .Selection(Sign_Bit), .Output(out_3));
endmodule

module Complementing_result (
  input  [31:0] Input,
  output [31:0] Output,
  output out_3
);

  wire [31:0] negator_1_out;

  Negator #(.width(32)) negator_1 (.in(Input), .out(negator_1_out));
  _32_bit_Mux_Module u_32_bit_mux_module_1 (
    .Input_0(Input), .Input_1(negator_1_out), .Selection(Input[31]), .Output(Output));

  assign out_3 = Input[31];
endmodule

module _4_Bit_Mux_Module (
  input  A0,
  input  A1,
  input  A2,
  input  A3,
  input  B0,
  input  B1,
  input  B2,
  input  B3,
  input  SELECTION,
  output _0,
  output _1,
  output _2,
  output _3
);

  // _74157 74157_1: pin names not known; wires that end beside it: SELECTION, A0, B0, _0, A1, B1, _1, 1'b0, 1'b1, 1'b0, A3, B3, _3, A2, B2, _2
endmodule

module _2_bit_Mux_Module (
  input  A0,
  input  A1,
  input  B0,
  input  B1,
  input  SELECTION,
  output out_6,
  output out_7
);

  // _74157 74157_1: pin names not known; wires that end beside it: SELECTION, A0, B0, out_6, A1, B1, out_7, 1'b0, 1'b1, 1'b0
endmodule

// MUX
module _10_Bit_Mux_Module (
  input  [9:0] B,
  input  SELECTION,
  input  [9:0] A,
  output [9:0] \output 
);

  _4_Bit_Mux_Module u_4_bit_mux_module_1 (
    .SELECTION(SELECTION), .A0(A[0]), .A1(A[1]), .A2(A[2]), .A3(A[3]), .B0(B[0]), .B1(B[1]), .B2(B[2]),
    .B3(B[3]), ._0(\output [0]), ._1(\output [1]), ._2(\output [2]), ._3(\output [3]));
  _4_Bit_Mux_Module u_4_bit_mux_module_2 (
    .SELECTION(SELECTION), .A0(A[4]), .A1(A[5]), .A2(A[6]), .A3(A[7]), .B0(B[4]), .B1(B[5]), .B2(B[6]),
    .B3(B[7]), ._0(\output [4]), ._1(\output [5]), ._2(\output [6]), ._3(\output [7]));
  _2_bit_Mux_Module u_2_bit_mux_module_1 (
    .SELECTION(SELECTION), .A0(A[8]), .A1(A[9]), .B0(B[8]), .B1(B[9]), .out_6(\output [8]),
    .out_7(\output [9]));

  // Notes on the sheet:
  //   A
endmodule

module Floating_Point_Adder (
  input  [31:0] A,
  input  [31:0] B,
  output OVERFLOW,
  output UNDERFLOW,
  output [31:0] RESULT
);

  main main_1 (
    .A(A), .B(B), .Result(RESULT), .Underflow(UNDERFLOW), .Overflow(OVERFLOW));  // open: Spectal_case_of_All_zero_output, Larger_Exponent, Smaller_Exponent_Significant, Difference_in_Exponent, Larger_Exponent_Significant, out_8, Storing_output_Sign_Bit, out_10, Output_fraction_after_1str_normalization, Exponent_after_1st_normalization, OF_after_1st_NRM, UF_after_1st_NRM, Output_fraction_after_2nd_normalization, Exponent_after_2nd_normalization, OF_after_2nd_NRM, UF_after_2nd_NRM
endmodule
