// Logisim project Rounding.circ as structural Verilog: 1 circuit, main circuit Rounding
module Rounding (
  input  [31:0] \input ,
  output [31:0] \output 
);

  wire n7432_1_p1, n7432_1_p3, n7432_1_p6, n7432_1_p7, n7432_2_p3, n7432_2_p6, n7432_2_p9;
  wire [0:0] n7408_1_p3;

  // _7432 7432_1: pin names not known; wires that end beside it: n7432_1_p1, \input [8], n7432_1_p3, n7432_1_p3, \input [6], n7432_1_p6, n7432_1_p7, \input [5], n7432_1_p1
  // _7408 7408_1: pin names not known; wires that end beside it: \input [7], n7432_1_p6, n7408_1_p3[0]
  // _7432 7432_2: pin names not known; wires that end beside it: \input [0], \input [1], n7432_2_p3, n7432_2_p3, \input [2], n7432_2_p6, n7432_2_p6, \input [3], n7432_2_p9, n7432_2_p9, \input [4], n7432_1_p7
  Adder #(.width(24)) adder_1 (
    .a(\input [31:8]), .b({{23{1'b0}}, n7408_1_p3[0]}), .out(\output [31:8]));  // open: cin, cout

  assign \output [7:0] = {8{1'b0}};

  // Notes on the sheet:
  //   Input 32 bit number
  //   P
  //   G
  //   R
  //   Sticky bits
  //   S
  //   Y=G.(P+S+R)
  //   Rounded Output 32 bit number
endmodule
