// Logisim project Data_Memory.circ as structural Verilog: 1 circuit, main circuit Data Memory
module Data_Memory (
  input  [3:0] Address,
  input  [3:0] Write_Data,
  input  MemWrite,
  input  CLK,
  input  MemRead,
  output [3:0] Output
);

  RAM #(.addrWidth(4), .dataWidth(4), .bus("separate")) ram_1 (
    .addr(Address), .din(Write_Data), .data(Output), .str(MemWrite), .clk(CLK), .ld(MemRead));  // open: sel, clr
endmodule
