// Logisim project Instruction_Memory.circ as structural Verilog: 1 circuit, main circuit Instruction Memory
// Instruction Address
module Instruction_Memory (
  input  [7:0] Read_Address,
  output [15:0] Instruction
);

  ROM #(.dataWidth(16)) rom_1 (.addr(Read_Address), .data(Instruction));  // open: sel

  // Notes on the sheet:
  //   contents of rom_1 (hex, n*v repeats v):
  //   e713 972e 120 8123 4014 d213 1221 7231 5160 3331 6224 777 777 5150 c020 b421 2115 777 a241 777 5160
  //   f028
endmodule
