// Logisim project MIPS.circ as structural Verilog: 1 circuit, main circuit main
module main (
  input  in_1
);

  wire and_1_out, and_2_out, clock_1_out, control_unit_1_alusrc, control_unit_1_beq, control_unit_1_bneq,
       control_unit_1_jump, control_unit_1_memread, control_unit_1_memtoreg, control_unit_1_memwrite,
       control_unit_1_regdst, control_unit_1_regwrite, main_1_value, main_2_zero, not_1_out, or_1_out;
  wire [2:0] control_unit_1_aluop;
  wire [3:0] data_memory_1_output, main_2_output, multiplexer_1_out, multiplexer_2_out, multiplexer_3_out,
       register_memory_1_p4, register_memory_1_p7, register_memory_1_p8;
  wire [7:0] adder_1_out, adder_2_out, instruction_memory_1_instruction, instruction_memory_1_instruction_2,
       multiplexer_4_out, multiplexer_6_out, register_1_q;

  Register register_1 (.D(multiplexer_6_out), .Q(register_1_q), .clk(clock_1_out), .clr(in_1));  // open: en
  Clock clock_1 (.out(clock_1_out));
  Instruction_Memory instruction_memory_1 (
    .Read_Address(register_1_q),
    .Instruction({instruction_memory_1_instruction_2, instruction_memory_1_instruction}));
  Multiplexer #(.width(4), .enable("false")) multiplexer_1 (
    .in0(instruction_memory_1_instruction[7:4]), .in1(instruction_memory_1_instruction[3:0]),
    .out(multiplexer_1_out), .sel(control_unit_1_regdst));
  Adder adder_1 (.a(register_1_q), .b(8'h1), .out(adder_1_out));  // open: cin, cout
  Control_Unit control_unit_1 (
    .Op_Code(instruction_memory_1_instruction_2[7:4]), .RegDst(control_unit_1_regdst),
    .Jump(control_unit_1_jump), .Beq(control_unit_1_beq), .Bneq(control_unit_1_bneq),
    .MemRead(control_unit_1_memread), .MemToReg(control_unit_1_memtoreg), .ALUOp(control_unit_1_aluop),
    .MemWrite(control_unit_1_memwrite), .ALUSrc(control_unit_1_alusrc), .RegWrite(control_unit_1_regwrite));
  // Register_Memory register_memory_1: pin names not known; wires that end beside it: instruction_memory_1_instruction_2[3:0], instruction_memory_1_instruction[7:4], multiplexer_1_out, register_memory_1_p4, control_unit_1_regwrite, clock_1_out, register_memory_1_p7, register_memory_1_p8
  Shift_Unit_main main_1 (.OpCode(instruction_memory_1_instruction_2[7:4]), .Value(main_1_value));
  Adder adder_2 (
    .a(adder_1_out), .b({instruction_memory_1_instruction_2[3:0], instruction_memory_1_instruction[7:4]}),
    .out(adder_2_out));  // open: cin, cout
  Multiplexer #(.width(4), .enable("false")) multiplexer_2 (
    .in0(register_memory_1_p8), .out(multiplexer_2_out), .sel(control_unit_1_alusrc));  // open: in1
  Multiplexer #(.width(4), .enable("false")) multiplexer_3 (
    .in0(register_memory_1_p7), .in1(instruction_memory_1_instruction[3:0]), .out(multiplexer_3_out),
    .sel(main_1_value));
  ALU_main main_2 (
    .Input_1(multiplexer_3_out), .Input_2(multiplexer_2_out), .ALUOp(control_unit_1_aluop),
    .Zero(main_2_zero), .Output(main_2_output));  // open: Overflow
  not not_1 (not_1_out, main_2_zero);
  and and_1 (and_1_out, control_unit_1_beq, main_2_zero);
  and and_2 (and_2_out, control_unit_1_bneq, not_1_out);
  Multiplexer #(.width(8), .enable("false")) multiplexer_4 (
    .in0(adder_1_out), .in1(adder_2_out), .out(multiplexer_4_out), .sel(or_1_out));
  or or_1 (or_1_out, and_1_out, and_2_out);
  Data_Memory data_memory_1 (
    .Address(main_2_output), .Output(data_memory_1_output), .MemWrite(control_unit_1_memwrite),
    .CLK(clock_1_out), .MemRead(control_unit_1_memread));  // open: Write_Data
  Multiplexer #(.width(4), .enable("false")) multiplexer_5 (
    .in0(main_2_output), .in1(data_memory_1_output), .out(register_memory_1_p4), .sel(control_unit_1_memtoreg));
  Multiplexer #(.width(8), .enable("false")) multiplexer_6 (
    .in0(multiplexer_4_out), .in1(instruction_memory_1_instruction_2), .out(multiplexer_6_out),
    .sel(control_unit_1_jump));

  // Notes on the sheet:
  //   Shift_unit
  //   Main ALU
endmodule
