// Logisim project MIPS_Final.circ as structural Verilog: 1 circuit, main circuit main
module main (
);

  wire CLK_out, control_unit_1_alusrc, control_unit_1_beq, control_unit_1_bneq, control_unit_1_jump,
       control_unit_1_memread, control_unit_1_memtoreg, control_unit_1_memwrite, control_unit_1_regdst,
       control_unit_1_regwrite, For_beq_out, For_bneq_out, MAIN_ALU_zero, not_1_out, or_1_out;
  wire [2:0] control_unit_1_aluop;
  wire [3:0] data_memory_1_output, MAIN_ALU_output, multiplexer_1_out, multiplexer_2_out, multiplexer_5_out,
       register_memory_1_read_1_data, register_memory_1_read_2_data;
  wire [7:0] adder_1_out, adder_2_out, instruction_memory_1_instruction_2, multiplexer_3_out,
       multiplexer_4_out, multiplexer_6_out, PC_q, subtractor_1_out;
  wire [15:0] instruction_memory_1_instruction;

  Register #(.trigger("falling")) PC (.D(multiplexer_6_out), .Q(PC_q), .clk(CLK_out), .clr(1'b0));  // open: en
  Clock CLK (.out(CLK_out));
  Instruction_Memory instruction_memory_1 (
    .Read_Address(PC_q),
    .Instruction({instruction_memory_1_instruction[15:12], instruction_memory_1_instruction_2, instruction_memory_1_instruction[3:0]}));
  Multiplexer #(.width(4), .enable("false")) multiplexer_1 (
    .in0(instruction_memory_1_instruction_2[3:0]), .in1(instruction_memory_1_instruction[3:0]),
    .out(multiplexer_1_out), .sel(control_unit_1_regdst));
  Adder adder_1 (.a(PC_q), .b(8'h1), .out(adder_1_out));  // open: cin, cout
  Control_Unit control_unit_1 (
    .Op_Code(instruction_memory_1_instruction[15:12]), .RegDst(control_unit_1_regdst),
    .Jump(control_unit_1_jump), .Beq(control_unit_1_beq), .Bneq(control_unit_1_bneq),
    .MemRead(control_unit_1_memread), .MemToReg(control_unit_1_memtoreg), .ALUOp(control_unit_1_aluop),
    .MemWrite(control_unit_1_memwrite), .ALUSrc(control_unit_1_alusrc), .RegWrite(control_unit_1_regwrite));
  Register_Memory register_memory_1 (
    .Read_1_Address(instruction_memory_1_instruction_2[7:4]), .RegWrite(control_unit_1_regwrite),
    .CLK(CLK_out), .Write_Address(multiplexer_1_out), .Read_1_Data(register_memory_1_read_1_data),
    .Read_2_Data(register_memory_1_read_2_data), .Write_Data(multiplexer_5_out),
    .Read_2_Address(instruction_memory_1_instruction_2[3:0]));
  Adder adder_2 (
    .a(adder_1_out), .b({4'b0000, instruction_memory_1_instruction[3:0]}), .out(adder_2_out));  // open: cin, cout
  Subtractor subtractor_1 (
    .a(adder_1_out), .b({4'b0000, instruction_memory_1_instruction[3:0]}), .out(subtractor_1_out));  // open: bin, bout
  Multiplexer #(.width(4), .enable("false")) multiplexer_2 (
    .in0(register_memory_1_read_2_data), .in1(instruction_memory_1_instruction[3:0]),
    .out(multiplexer_2_out), .sel(control_unit_1_alusrc));
  Multiplexer #(.width(8), .enable("false")) multiplexer_3 (
    .in0(adder_2_out), .in1(subtractor_1_out), .out(multiplexer_3_out),
    .sel(instruction_memory_1_instruction[3]));
  ALU_main MAIN_ALU (
    .Input_1(register_memory_1_read_1_data), .Input_2(multiplexer_2_out), .ALUOp(control_unit_1_aluop),
    .Zero(MAIN_ALU_zero), .Output(MAIN_ALU_output));  // open: Overflow
  not not_1 (not_1_out, MAIN_ALU_zero);
  and For_beq (For_beq_out, control_unit_1_beq, MAIN_ALU_zero);
  and For_bneq (For_bneq_out, control_unit_1_bneq, not_1_out);
  Multiplexer #(.width(8), .enable("false")) multiplexer_4 (
    .in0(adder_1_out), .in1(multiplexer_3_out), .out(multiplexer_4_out), .sel(or_1_out));
  or or_1 (or_1_out, For_beq_out, For_bneq_out);
  Data_Memory data_memory_1 (
    .Address(MAIN_ALU_output), .Write_Data(register_memory_1_read_2_data), .Output(data_memory_1_output),
    .MemWrite(control_unit_1_memwrite), .CLK(CLK_out), .MemRead(control_unit_1_memread));
  Multiplexer #(.width(4), .enable("false")) multiplexer_5 (
    .in0(MAIN_ALU_output), .in1(data_memory_1_output), .out(multiplexer_5_out), .sel(control_unit_1_memtoreg));
  Multiplexer #(.width(8), .enable("false")) multiplexer_6 (
    .in0(multiplexer_4_out), .in1(instruction_memory_1_instruction_2), .out(multiplexer_6_out),
    .sel(control_unit_1_jump));
endmodule
