// Logisim project Shift-Unit.circ as structural Verilog: 1 circuit, main circuit main
module main (
  input  [3:0] OpCode,
  output Value
);

  wire and_1_out, and_2_out, not_1_out, not_2_out, not_3_out, not_4_out, not_5_out;

  not not_1 (not_1_out, OpCode[1]);
  not not_2 (not_2_out, OpCode[2]);
  not not_3 (not_3_out, OpCode[3]);
  not not_4 (not_4_out, OpCode[2]);
  not not_5 (not_5_out, OpCode[3]);
  and and_1 (and_1_out, OpCode[0], not_1_out, not_2_out, not_3_out);
  and and_2 (and_2_out, OpCode[0], OpCode[1], not_4_out, not_5_out);
  or or_1 (Value, and_1_out, and_2_out);

  // Notes on the sheet:
  //   Shift unit might need to be changed based on our ISA
endmodule
